# Fritzing sketch elshema (saved by Fritzing 0.9.2b)
breadboards: 1

parts:
  Част1 = Arduino Uno (Rev3)
  R1 = Resistor [tolerance=±5% resistance=22k package=THT]
  R2 = Resistor [tolerance=±5% resistance=22k package=THT]
  U1 = ACS712 [package=so08]
  R3 = Resistor [tolerance=±5% resistance=10k package=THT]
  S1 = Toggle Switch [package=THT]

nets:
  N1: Част1.A0, S1.L2
  N2: Част1.A1, R1.Pin_1, R2.Pin_0
  N3: Част1.A2, U1.VOUT
  GND/Rx: Част1.A3, R2.Pin_1, U1.GND, R3.Pin_1
  N4: R1.Pin_0, S1.L1
  I+: U1.IP+
  I-: U1.IP-
  5V: U1.VCC
  Uin: S1.COM
